# Fritzing sketch Sketch (saved by Fritzing 0.9.3b)
breadboards: 1

parts:
  Composant1 = Arduino Leonardo (Rev3b)
  Composant2 = Barometric Pressure Sensor - BMP180 Breakout (GY-68)

nets:
  N1: Composant1.D2/SDA, Composant2.SDA
  N2: Composant1.D3_PWM/SCL, Composant2.SCL
  5V: Composant1.5V, Composant2.VCC
  GND: Composant1.GND, Composant2.GND

notes:
  SDA/SDI
  SCL/SCK
  VCC
  GND
  The sensor pictured here is a BMP180 but it's the same for a BME280
