# Fritzing sketch Sketch (saved by Fritzing 0.9.9b)
breadboards: 1

parts:
  LCD1 = 2.8" SPI TFT Module [part_number=MSP2807]
  Part1 = Arduino Leonardo (Rev3b)
  R1 = Resistor [tolerance=±5% power=0.25 resistance=10k package=THT]
  R2 = Resistor [tolerance=±5% power=0.25 resistance=10k package=THT]
  R3 = Resistor [tolerance=±5% power=0.25 resistance=10k package=THT]
  R4 = Resistor [tolerance=±5% power=0.25 resistance=10k package=THT]
  R5 = Resistor [tolerance=±5% power=0.25 resistance=10k package=THT]

nets:
  N1: LCD1.pin1, LCD1.pin8, Part1.5V
  N2: LCD1.pin2, Part1.GND
  N3: LCD1.pin3, R1.Pin_0
  N4: LCD1.pin4, R2.Pin_0
  N5: LCD1.pin5, R3.Pin_0
  N6: LCD1.pin6, R4.Pin_0
  N7: LCD1.pin7, R5.Pin_0
  N8: LCD1.pin9, Part1.D12/A11
  N9: Part1.D8/A8, R1.Pin_1
  N10: Part1.D9_PWM/A9, R2.Pin_1
  N11: Part1.D10_PWM/A10, R3.Pin_1
  N12: Part1.D11_PWM, R4.Pin_1
  N13: Part1.D13_PWM, R5.Pin_1

notes:
  MISO (SDO)
  LED
  SCK
  MOSI (SDI)
  DC
  RESET
  CS
  GND
  VCC

custom parts:
  2.8" SPI TFT Module: A generic 2.8 inch LCD TFT 320x240 display with touchscreen and SD card slot. Uses the ILI9341 controller, like the Adafruit displays of this size uses.
