# Fritzing sketch Arduino Leonardo WS2812 array (saved by Fritzing 0.9.3b)

parts:
  Leonardo = Arduino Leonardo (Rev3b)
  LED4 = ws2812b [package="smd 2812b"]
  LED9 = ws2812b [package="smd 2812b"]
  LED5 = ws2812b [package="smd 2812b"]
  LED8 = ws2812b [package="smd 2812b"]
  LED3 = ws2812b [package="smd 2812b"]
  LED2 = ws2812b [package="smd 2812b"]
  LED1 = ws2812b [package="smd 2812b"]
  LED6 = ws2812b [package="smd 2812b"]
  LED7 = ws2812b [package="smd 2812b"]

nets:
  N1: Leonardo.D7, LED1.DIN
  VDD: Leonardo.5V, LED4.VDD, LED9.VDD, LED5.VDD, LED8.VDD, LED3.VDD, LED2.VDD, LED1.VDD, LED6.VDD, LED7.VDD
  VSS: Leonardo.GND, LED4.VSS, LED9.VSS, LED5.VSS, LED8.VSS, LED3.VSS, LED2.VSS, LED1.VSS, LED6.VSS, LED7.VSS
  N2: LED4.DOUT, LED5.DIN
  N3: LED4.DIN, LED3.DOUT
  N4: LED9.DIN, LED8.DOUT
  N5: LED5.DOUT, LED6.DIN
  N6: LED8.DIN, LED7.DOUT
  N7: LED3.DIN, LED2.DOUT
  N8: LED2.DIN, LED1.DOUT
  N9: LED6.DOUT, LED7.DIN

notes:
  Example array of 3x3 WS2812 RGB LEDs
  Connected to a Leonardo
  Array can be of any size, as long as LEDs are connected properly together to form a chain.
  Careful with how much power the LEDs drain from the Arduino, you can max out the max amperage of the 5V output if there are too many LEDs.
