# Fritzing sketch Sketch (saved by Fritzing 0.9.3b)
breadboards: 1

parts:
  R1 = Resistor [tolerance=±5% resistance=220 package="0402 [SMD]"]
  Composant1 = Arduino Leonardo (Rev3b)
  LED1 = RGB LED (com. anode, rbg) [package="5 mm [THT]"]
  R2 = Resistor [tolerance=±5% resistance=220 package="0402 [SMD]"]
  R3 = Resistor [tolerance=±5% resistance=220 package="0402 [SMD]"]
  RE2 = Rotary Encoder [package=THT]
  S1 = Pushbutton [package="[SMD]"]

nets:
  N1: R1.Pin_0, LED1.red_cathode
  N2: R1.Pin_1, Composant1.D9_PWM/A9
  N3: Composant1.D0/RX, RE2.EncoderPinA
  N4: Composant1.D1/TX, RE2.EncoderPinB
  N5: Composant1.D2/SDA, S1.Pin_1, S1.Pin_2
  N6: Composant1.5V, LED1.common_anode
  N7: Composant1.GND, RE2.EncoderPinC, S1.Pin_3, S1.Pin_4
  N8: Composant1.D10_PWM/A10, R2.Pin_1
  N9: Composant1.D11_PWM, R3.Pin_1
  N10: LED1.blue_cathode, R2.Pin_0
  N11: LED1.green_cathode, R3.Pin_0
