# Fritzing sketch Sketch (saved by Fritzing 0.9.3b)
breadboards: 1

parts:
  Composant1 = Arduino Leonardo (Rev3b)
  LED1 = RGB LED (com. anode, rbg) [package="5 mm [THT]"]
  R1 = Resistor [tolerance=±5% resistance=330 package="0402 [SMD]"]
  R2 = Resistor [tolerance=±5% resistance=330 package="0402 [SMD]"]
  R3 = Resistor [tolerance=±5% resistance=330 package="0402 [SMD]"]

nets:
  N1: Composant1.5V, LED1.common_anode
  N2: Composant1.D9_PWM/A9, R1.Pin_1
  N3: Composant1.D10_PWM/A10, R2.Pin_1
  N4: Composant1.D11_PWM, R3.Pin_1
  N5: LED1.red_cathode, R1.Pin_0
  N6: LED1.blue_cathode, R2.Pin_0
  N7: LED1.green_cathode, R3.Pin_0

notes:
  We're using a common anode LED that needs +5V. Common cathode needs GND.
