# Fritzing sketch Sketch (saved by Fritzing 0.9.3b)
breadboards: 1

parts:
  Composant1 = sx1509 breakout
  Composant2 = Arduino Leonardo (Rev3b)
  S1 = Momentary Switch [package=ksa_sealed_tac_switch]

nets:
  GND: Composant1.GND, Composant2.GND, S1.2
  3.3V: Composant1.3.3V, Composant2.3V3
  N1: Composant1.SDA, Composant2.D2/SDA, Composant2.SDA
  N2: Composant1.SCL, Composant2.D3_PWM/SCL, Composant2.SCL
  N3: Composant1.0, S1.3
