# Fritzing sketch Sketch (saved by Fritzing 0.9.3b)
breadboards: 1

parts:
  Composant1 = Arduino Leonardo (Rev3b)
  LED1 = LEDs [package=led10mm]
  R1 = Resistor [tolerance=±5% resistance=220 package="1206 [SMD]"]

nets:
  N1: Composant1.GND, LED1.C
  N2: Composant1.D11_PWM, R1.Pin_0
  N3: LED1.A, R1.Pin_1
