# Fritzing sketch Sketch (saved by Fritzing 0.9.3b)
breadboards: 1

parts:
  Composant1 = Arduino Leonardo (Rev3b)
  RE1 = Rotary Encoder [package=THT]
  OLED1 = OLED 128x32 I2C Monochrome Display

nets:
  N1: Composant1.D2/SDA, OLED1.SDA
  N2: Composant1.D3_PWM/SCL, OLED1.SCK
  3V3: Composant1.3V3, OLED1.VDD
  N3: Composant1.D9_PWM/A9, RE1.EncoderPinB
  N4: Composant1.D10_PWM/A10, RE1.EncoderPinA
  GND: Composant1.GND, RE1.EncoderPinC, OLED1.GND
