# Fritzing sketch Arduino Leonardo - Rotary Encoder (saved by Fritzing 0.9.3b)
breadboards: 1

parts:
  Composant1 = Arduino Leonardo (Rev3b)
  RE1 = Rotary Encoder [package=THT]
  RE2 = Rotary Encoder [package=THT]

nets:
  N1: Composant1.D0/RX, RE1.EncoderPinB
  N2: Composant1.D1/TX, RE1.EncoderPinA
  N3: Composant1.GND, RE1.EncoderPinC, RE2.EncoderPinC
  N4: Composant1.D9_PWM/A9, RE2.EncoderPinB
  N5: Composant1.D10_PWM/A10, RE2.EncoderPinA

notes:
  Rotary encoders can have different pins orders. Make sure:
  - pin A -> D0
  - pin B -> D1
  - pin C -> GND
