# Fritzing sketch Sketch (saved by Fritzing 0.9.3b)
breadboards: 1

parts:
  Composant1 = Arduino Leonardo (Rev3b)
  OLED3 = OLED 128x32 I2C Monochrome Display

nets:
  N1: Composant1.D2/SDA, OLED3.SDA
  N2: Composant1.D3_PWM/SCL, OLED3.SCK
  3V3: Composant1.3V3, OLED3.VDD
  GND: Composant1.GND, OLED3.GND
