# Fritzing sketch Sketch (saved by Fritzing 0.9.3b)

parts:
  Composant1 = Arduino Leonardo (Rev3b)
  OLED1 = OLED 128x64 I2C Monochrome Display

nets:
  N1: Composant1.D2/SDA, OLED1.SDA
  N2: Composant1.D3_PWM/SCL, OLED1.SCK
  3V3: Composant1.3V3, OLED1.VDD
  GND: Composant1.GND, OLED1.GND

notes:
  We could use the dedicated SCL and SDA pins on the Leonardo but some libs don't like that and won't work properly
