# Fritzing sketch Arduino Leonardo - Potentiometer Slider (saved by Fritzing 0.9.3b)

parts:
  R1 = Slide Potentiometer [maximum_resistance=100kΩ]
  Composant1 = Arduino Leonardo (Rev3b)

nets:
  N1: R1.leg1, Composant1.5V
  N2: R1.wiper, Composant1.A0
  N3: R1.leg2, Composant1.GND

notes:
  Sliding potentiometers can have a different pinout. Make sure to check your potentiometer schematic before wiring everything.
